# Fritzing sketch SmartGarden (saved by Fritzing 0.9.4)
circuit board: 7.16444cm x 6.39121cm
breadboards: 1

parts:
  Pico = Raspberry Pi Pico
  R1 = Photocell (LDR) [package=THT]
  LED1 = LED - 5mm [color="Red (633nm)" package="5 mm [THT]"]
  S1 = Round Pushbutton
  S2 = Round Pushbutton
  S3 = Round Pushbutton
  S4 = Round Pushbutton
  S5 = Round Pushbutton
  S6 = Round Pushbutton
  S8 = Round Pushbutton
  S10 = Round Pushbutton
  S11 = Round Pushbutton
  S12 = Round Pushbutton
  S13 = Round Pushbutton
  S14 = Round Pushbutton
  S15 = Round Pushbutton
  S16 = Round Pushbutton
  R2 = Resistor [tolerance=±5% resistance=330 package=THT]
  BATT = DC Power [voltage=5]
  Part2 = NRF24L01+ Breakout Board
  DHT1 = DHT11 Humitidy and Temperature Sensor
  Capacitive_Soil_Moisture_Sensor1 = DFRobot Capacitive Soil Moisture Sensor V1.0 [part_number=SEN0193]
  S9 = Round Pushbutton
  S7 = Round Pushbutton

nets:
  N1: Pico.pin_1, Part2.MISO
  N2: Pico.pin_2, Part2.CS
  N3: Pico.pin_3, Pico.pin_8, Pico.pin_13, Pico.pin_18, Pico.pin_23, Pico.pin_28, Pico.pin_33, Pico.pin_38
  N4: Pico.pin_4, Part2.SCK
  N5: Pico.pin_5, Part2.MOSI
  N6: Pico.pin_6, DHT1.DATA
  N7: Pico.pin_7, S1.leg1
  N8: Pico.pin_9, S2.leg1
  N9: Pico.pin_10, S3.leg1
  N10: Pico.pin_11, S4.leg1
  N11: Pico.pin_12, S5.leg1
  N12: Pico.pin_14, S6.leg1
  N13: Pico.pin_15, S7.leg1
  N14: Pico.pin_16, S8.leg1
  N15: Pico.pin_17, S9.leg1
  N16: Pico.pin_19, S10.leg1
  N17: Pico.pin_21, S11.leg1
  N18: Pico.pin_22, S12.leg1
  N19: Pico.pin_24, S13.leg1
  N20: Pico.pin_25, S14.leg1
  N21: Pico.pin_26, S15.leg1
  N22: Pico.pin_27, S16.leg1
  N23: Pico.pin_29, R2.Pin_0
  N24: Pico.pin_31, R1.pin_0
  N25: Pico.pin_32, Capacitive_Soil_Moisture_Sensor1.A
  N26: Pico.pin_34, Pico.pin_39, BATT.V+
  5V: Pico.pin_35, R1.pin_1, Part2.VCC, DHT1.VDD, Capacitive_Soil_Moisture_Sensor1.VCC
  GND: Pico.pin_37, LED1.cathode, LED1.anode, S1.leg0, S2.leg0, S3.leg0, S4.leg0, S5.leg0, S6.leg0, S8.leg0, S10.leg0, S11.leg0, S12.leg0, S13.leg0, S14.leg0, S15.leg0, S16.leg0, R2.Pin_1, BATT.V-, Part2.GND, Part2.CE, Part2.IRQ, DHT1.NULL, DHT1.GND, Capacitive_Soil_Moisture_Sensor1.GND, S9.leg0, S7.leg0

notes:
  Pull Ups? Check Miso and MOSI?
  Does onewire pin matter?

custom parts:
  Raspberry Pi Pico: Raspberry Pi Pico. Based around the RP2040 microcontroller the Pico is a low cost microcontroller device bringing Raspberry Pi quality, cost, and easy of use to the microcontroller space. Jan 2021, Split part in to two versions: tht (this one) and SMD. This one will drill holes for a .1 in header in pcb to allow plugging in the module as well as providing pads to solder the module to the top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
  DHT11 Humitidy and Temperature Sensor: DHT11 Humidity and Temperature Sensor
  DFRobot Capacitive Soil Moisture Sensor V1.0: DFRobot Capacitive Soil Moisture Sensor V1.0 This product measures soil moisture levels by capacitive sensing, rather than resistive sensing like other types of moisture sensor. It is made of a corrosion resistant material giving it a long service life. Insert it into soil and impress your friends with the real-time soil moisture data! The product includes an on-board voltage regulator which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
